// Logisim project lab 4.circ as structural Verilog: 2 circuits, main circuit RS
module RS (
  input  in_1,
  input  in_2,
  input  in_3,
  input  in_4,
  input  in_5,
  input  in_6,
  input  in_7,
  output out_8,
  output out_9,
  output out_10,
  output out_11,
  output out_12,
  output out_13
);

  wire nand_3_out, nand_4_out;

  nor nor_1 (out_8, in_1, out_9);
  nor nor_2 (out_9, out_8, in_2);
  nand nand_1 (out_10, in_3, out_11);
  nand nand_2 (out_11, out_10, in_4);
  nand nand_3 (nand_3_out, in_5, in_6);
  nand nand_4 (nand_4_out, in_6, in_7);
  nand nand_5 (out_12, nand_3_out, out_13);
  nand nand_6 (out_13, out_12, out_12, nand_4_out);
endmodule

module S_R_E (
  input  in_1,
  input  in_2,
  input  in_3,
  input  in_4,
  input  in_5,
  input  in_6,
  output out_7,
  output out_8,
  output out_9,
  output out_10,
  output out_11,
  output out_12
);

  wire nand_1_out, nand_2_out, nand_3_out, nand_4_out, nand_5_out, nand_6_out, nand_11_out, nand_12_out;

  nand nand_1 (nand_1_out, in_1, in_1);
  nand nand_2 (nand_2_out, nand_1_out, in_2);
  nand nand_3 (nand_3_out, in_3, nand_4_out);
  nand nand_4 (nand_4_out, in_4, in_4);
  nand nand_5 (nand_5_out, in_5, in_5);
  nand nand_6 (nand_6_out, in_6, in_6);
  nand nand_7 (out_7, nand_1_out, out_8);
  nand nand_8 (out_8, out_7, nand_2_out);
  nand nand_9 (out_9, nand_3_out, nand_3_out, out_10);
  nand nand_10 (out_10, out_9, nand_4_out);
  nand nand_11 (nand_11_out, in_5, nand_6_out);
  nand nand_12 (nand_12_out, nand_5_out, in_6);
  nand nand_13 (out_11, nand_11_out, out_12);
  nand nand_14 (out_12, out_11, nand_12_out);
endmodule
