// Logisim project lab 5.circ as structural Verilog: 1 circuit, main circuit T D
module T_D (
  input  in_1,
  input  in_2,
  input  in_3,
  input  in_4,
  output out_5,
  output out_6,
  output out_7
);

  wire d_ff_1_qn, nand_1_out, nand_2_out, nand_3_out;

  nand nand_1 (nand_1_out, in_1, in_2);
  nand nand_2 (nand_2_out, in_3, in_4);
  nand nand_3 (nand_3_out, nand_2_out, in_4);
  D_Flip_Flop d_ff_1 (.clk(d_ff_1_qn), .D(nand_1_out), .Q(out_5), .Qn(d_ff_1_qn));  // open: preset, en, reset
  nand nand_4 (out_6, nand_2_out, out_7);
  nand nand_5 (out_7, out_6, nand_3_out);
endmodule
