// Logisim project lab 6.circ as structural Verilog: 6 circuits, main circuit Схема сравнения
module \Схема_сравнения  (
  input  X1,
  input  X2,
  output Y
);

  wire and_1_out, and_2_out, not_1_out, not_2_out;

  not not_1 (not_1_out, X1);
  not not_2 (not_2_out, X2);
  and and_1 (and_1_out, not_1_out, X2);
  and and_2 (and_2_out, X1, not_2_out);
  or or_1 (Y, and_1_out, and_2_out);
endmodule

module \Полусумматор  (
  input  X1,
  input  X2,
  output \старший ,
  output \младший 
);

  and and_1 (\старший , X1, X2);
  \Схема_сравнения  \u_Сх_сравнения  (.X1(X1), .X2(X2), .Y(\младший ));
endmodule

// sm
module \Полный_сумматор  (
  input  X1,
  input  X2,
  input  Pi,
  output p,
  output s
);

  wire \полусумматор_1_младший , \полусумматор_1_старший , \полусумматор_2_старший ;

  \Полусумматор  \u_полусумматор_1  (
    .X1(X1), .X2(X2), .\старший (\полусумматор_1_старший ), .\младший (\полусумматор_1_младший ));
  \Полусумматор  \u_полусумматор_2  (
    .X1(\полусумматор_1_младший ), .X2(Pi), .\старший (\полусумматор_2_старший ), .\младший (s));
  or or_1 (p, \полусумматор_1_старший , \полусумматор_2_старший );
endmodule

module \_4_сумматора  (
  input  X4,
  input  Y4,
  input  X3,
  input  Y3,
  input  X2,
  input  Y2,
  input  X1,
  input  Y1,
  input  P0,
  output S5,
  output S4,
  output S3,
  output S2,
  output S1
);

  wire \полный_сумматор_1_p , \полный_сумматор_2_p , \полный_сумматор_3_p ;

  \Полный_сумматор  \u_полный_сумматор_1  (
    .X1(X2), .X2(Y2), .Pi(\полный_сумматор_2_p ), .p(\полный_сумматор_1_p ), .s(S2));
  \Полный_сумматор  \u_полный_сумматор_2  (.X1(X1), .X2(Y1), .Pi(P0), .p(\полный_сумматор_2_p ), .s(S1));
  \Полный_сумматор  \u_полный_сумматор_3  (
    .X1(X3), .X2(Y3), .Pi(\полный_сумматор_1_p ), .p(\полный_сумматор_3_p ), .s(S3));
  \Полный_сумматор  \u_полный_сумматор_4  (.X1(X4), .X2(Y4), .Pi(\полный_сумматор_3_p ), .p(S5), .s(S4));
endmodule

module \Полусумматор__из_теоретического_раздела  (
  input  A,
  input  B,
  output S,
  output P
);

  wire not_1_out, or_1_out;

  or or_1 (or_1_out, A, B);
  and and_1 (P, A, B, B);
  not not_1 (not_1_out, P);
  and and_2 (S, or_1_out, not_1_out);
endmodule

module \Сумматор__из_теоретического_раздела  (
  input  A,
  input  B,
  input  P0,
  output P,
  output S
);

  wire and_1_out, and_2_out, and_3_out, and_4_out, and_5_out, not_1_out, or_1_out;

  and and_1 (and_1_out, A, B);
  and and_2 (and_2_out, A, P0);
  and and_3 (and_3_out, B, P0);
  or or_1 (or_1_out, A, B, P0);
  and and_4 (and_4_out, A, B, P0);
  or or_2 (P, and_1_out, and_2_out, and_3_out);
  not not_1 (not_1_out, P);
  and and_5 (and_5_out, not_1_out, or_1_out);
  or or_3 (S, and_5_out, and_4_out);
endmodule
