// Logisim project lab 7.circ as structural Verilog: 5 circuits, main circuit 2х канальный мультиплексор
module \_2х_канальный_мультиплексор  (
  input  a,
  input  b,
  input  sel,
  output out
);

  wire and_1_out, and_2_out, not_1_out;

  not not_1 (not_1_out, sel);
  and and_1 (and_1_out, a, not_1_out);
  and and_2 (and_2_out, b, sel);
  or or_1 (out, and_1_out, and_2_out);
endmodule

module \_4х_канальный_мультиплексор  (
  input  a0,
  input  d0,
  input  a1,
  input  d1,
  input  d2,
  input  d3,
  output y
);

  wire and_1_out, and_2_out, and_3_out, and_4_out, not_1_out, not_2_out;

  not not_1 (not_1_out, a0);
  not not_2 (not_2_out, a1);
  and and_1 (and_1_out, not_1_out, d0, not_2_out);
  and and_2 (and_2_out, not_2_out, d1, d1, a0);
  and and_3 (and_3_out, not_1_out, d2, a1);
  and and_4 (and_4_out, a1, d3, a0);
  or or_1 (y, and_1_out, and_2_out, and_3_out, and_4_out);
endmodule

module \_16ти_канальный_мультиплексор  (
  input  D0,
  input  D1,
  input  D2,
  input  D3,
  input  D4,
  input  D5,
  input  D6,
  input  D7,
  input  D8,
  input  D9,
  input  D10,
  input  D11,
  input  D12,
  input  D13,
  input  D14,
  input  D15,
  input  A0,
  input  A1,
  input  A2,
  input  A3,
  output out_21
);

  wire \n4х_канальный_мультиплексор_1_y , \n4х_канальный_мультиплексор_2_y ,
       \n4х_канальный_мультиплексор_3_y , \n4х_канальный_мультиплексор_4_y ;

  \_4х_канальный_мультиплексор  \u_4х_канальный_мультиплексор_1  (
    .a0(A0), .d0(A1), .a1(D0), .d1(D1), .d2(D2), .d3(D2), .y(\n4х_канальный_мультиплексор_1_y ));
  \_4х_канальный_мультиплексор  \u_4х_канальный_мультиплексор_2  (
    .a0(A0), .d0(A1), .a1(D4), .d1(D5), .d2(D6), .d3(D7), .y(\n4х_канальный_мультиплексор_2_y ));
  \_4х_канальный_мультиплексор  \u_4х_канальный_мультиплексор_3  (
    .a0(A0), .d0(A1), .a1(D8), .d1(D9), .d2(D10), .d3(D11), .y(\n4х_канальный_мультиплексор_3_y ));
  \_4х_канальный_мультиплексор  \u_4х_канальный_мультиплексор_4  (
    .a0(A0), .d0(A1), .a1(D12), .d1(D13), .d2(D14), .d3(D15), .y(\n4х_канальный_мультиплексор_4_y ));
  \_4х_канальный_мультиплексор  \u_4х_канальный_мультиплексор_5  (
    .a0(A2), .d0(A3), .a1(\n4х_канальный_мультиплексор_1_y ), .d1(\n4х_канальный_мультиплексор_2_y ),
    .d2(\n4х_канальный_мультиплексор_3_y ), .d3(\n4х_канальный_мультиплексор_4_y ), .y(out_21));

  assign D3 = D2;
endmodule

module \_16ти_канальный_мультиплексор__стандартные_элементы_Logisim  (
  input  D0,
  input  D1,
  input  D2,
  input  D3,
  input  D4,
  input  D5,
  input  D6,
  input  D7,
  input  D8,
  input  D9,
  input  D10,
  input  D11,
  input  D12,
  input  D13,
  input  D14,
  input  D15,
  input  [3:0] in_17,
  output out_18
);

  wire [3:0] undriven;

  Multiplexer #(.select(4), .enable("false")) multiplexer_1 (
    .in0(D0), .in1(D1), .in2(D2), .in3(D3), .in4(D4), .in5(D5), .in6(D6), .in7(D7), .in8(D8), .in9(D9),
    .in10(D10), .in11(D11), .in12(D12), .in13(D13), .in14(D14), .in15(D15), .out(out_18), .sel(undriven));
endmodule

module \Демультиплексор  (
  input  IN,
  input  SEL,
  output A,
  output B
);

  wire not_1_out;

  not not_1 (not_1_out, SEL);
  and and_1 (A, IN, not_1_out);
  and and_2 (B, IN, SEL);
endmodule
