// Logisim project lab 8.circ as structural Verilog: 1 circuit, main circuit main
module main (
);

  wire and_1_out, and_2_out, and_3_out, button_1_out, button_2_out, not_1_out, not_2_out, not_3_out;
  wire [2:0] counter_1_q, ram_1_data;
  wire [3:0] counter_2_q, multiplexer_1_out, register_2_q, register_3_q;
  wire [7:0] adder_1_out, adder_2_out, multiplexer_2_out, multiplexer_3_out, ram_2_data, ram_3_data,
       register_1_q, register_4_q, register_5_q;

  Counter #(.width(3), .max('h7)) counter_1 (.Q(counter_1_q), .clk(button_1_out));  // open: load, D, count, carry, clr
  Button button_1 (.out(button_1_out));
  not not_1 (not_1_out, button_1_out);
  Counter #(.width(4), .max('hf)) counter_2 (
    .load(register_3_q[3]), .D(register_2_q), .count(not_2_out), .Q(counter_2_q), .clk(button_2_out));  // open: carry, clr
  not not_2 (not_2_out, register_3_q[3]);
  Button button_2 (.out(button_2_out));
  Multiplexer #(.width(4)) multiplexer_1 (
    .in0(counter_2_q), .in1(register_2_q), .out(multiplexer_1_out), .sel(not_3_out));  // open: en
  not not_3 (not_3_out, button_2_out);
  RAM #(.addrWidth(3), .dataWidth(3), .bus("separate")) ram_1 (
    .addr(counter_1_q), .data(ram_1_data));  // open: din, str, sel, clk, ld, clr
  and and_1 (and_1_out, button_2_out, register_3_q[1]);
  RAM #(.addrWidth(4), .bus("separate")) ram_2 (
    .addr(multiplexer_1_out), .din(register_5_q), .data(ram_2_data), .clk(and_1_out));  // open: str, sel, ld, clr
  // Probe on ram_3_data
  RAM #(.addrWidth(3), .bus("separate")) ram_3 (
    .addr(counter_1_q), .din(register_4_q), .data(ram_3_data), .clk(ram_1_data[1]));  // open: str, sel, ld, clr
  Register #(.trigger("falling")) register_1 (.D(ram_2_data), .Q(register_1_q), .clk(and_3_out));  // open: en, clr
  // Probe on register_1_q
  Register #(.width(4)) register_2 (.D(ram_2_data[3:0]), .Q(register_2_q), .clk(not_3_out));  // open: en, clr
  Adder adder_1 (.a(register_4_q), .b(ram_3_data), .out(adder_1_out));  // open: cin, cout
  Adder adder_2 (.a(register_5_q), .b(register_1_q), .out(adder_2_out));  // open: cin, cout
  // Probe on adder_2_out
  Register #(.width(4)) register_3 (.D(ram_2_data[7:4]), .Q(register_3_q), .clk(not_3_out));  // open: en, clr
  // Probe on adder_1_out
  Multiplexer #(.width(8)) multiplexer_2 (
    .in0(adder_1_out), .in1(ram_3_data), .out(multiplexer_2_out), .sel(ram_1_data[2]));  // open: en
  and and_2 (and_2_out, ram_1_data[0], not_1_out);
  Multiplexer #(.width(8)) multiplexer_3 (
    .in0(adder_2_out), .in1(register_1_q), .out(multiplexer_3_out), .sel(register_3_q[2]));  // open: en
  and and_3 (and_3_out, register_3_q[0], not_3_out);
  Register register_4 (.D(multiplexer_2_out), .Q(register_4_q), .clk(and_2_out));  // open: en, clr
  Register #(.trigger("falling")) register_5 (
    .D(multiplexer_3_out), .Q(register_5_q), .clk(button_2_out));  // open: en, clr

  // Notes on the sheet:
  //   Команды
  //   Данные
  //   Temp
  //   Adress
  //   Instruction
  //   Acc
endmodule
